// Logisim project proj2.circ as structural Verilog: 20 circuits, main circuit Main
module Main (
  input  Reset,
  output Z,
  output C,
  output N,
  output V,
  output [15:0] NextPC,
  output [15:0] ALUOut
);

  wire branchenableunit_1_out_4, branchmuxdecoder_1_out_2, branchrequestunit_1_brreq, Clock_out, CondUpdate,
       MemRead, MemWrite, RegWrite;
  wire [2:0] ASel, branchrequestunit_1_brtype, BSel, WSel;
  wire [3:0] n16_bit_alu_1_out_5;
  wire [4:0] ALUOp, Imm5;
  wire [7:0] Imm8;
  wire [10:0] Imm11;
  wire [15:0] ABus, AOut, BBus, BOut, CurrPC, DataOut, Inst, MulOut, multiplexer_2_out, multiplexer_3_out,
       pc_control_unit_1_nextpc, ShiftOut, WIn, WOut;

  Register #(.width(16)) register_1 (.D(NextPC), .Q(CurrPC), .clk(Clock_out), .clr(Reset));  // open: en
  Clock Clock (.out(Clock_out));
  Decoder decoder_1 (
    .ALUOp(ALUOp), .Inst(Inst), .Cond__Update(CondUpdate), .MemRead(MemRead), .MemWrite(MemWrite),
    .RegWrite(RegWrite), .WSel(WSel), .ASel(ASel), .BSel(BSel), .Imm5(Imm5), .Imm8(Imm8), .Imm11(Imm11));
  RAM #(.addrWidth(16), .dataWidth(16), .bus("asynch")) ram_1 (
    .addr(CurrPC), .data(Inst), .clr(Reset));  // open: sel, ld
  BranchRequestUnit branchrequestunit_1 (
    .Op(ALUOp), .BrReq(branchrequestunit_1_brreq), .BrType(branchrequestunit_1_brtype));
  PC_Control_Unit pc_control_unit_1 (
    .CurPC(CurrPC), .Imm(BBus), .PCSel(branchenableunit_1_out_4), .NextPC(pc_control_unit_1_nextpc));
  BranchEnableUnit branchenableunit_1 (
    .BrType(branchrequestunit_1_brtype), .BranchReq(branchrequestunit_1_brreq),
    .CondCodes__ZCNV({V, N, C, Z}), .out_4(branchenableunit_1_out_4));
  Register_File register_file_1 (
    .WData(WIn), .Clk(Clock_out), ._0(Reset), .WEn(RegWrite), .ABus(AOut), .ASel(ASel), .BBus(BOut),
    .BSel(BSel), .WBus(WOut), .WSel(WSel));
  Multiplexer #(.width(16), .enable("false")) multiplexer_1 (
    .in0(pc_control_unit_1_nextpc), .in1(ABus), .out(NextPC), .sel(branchmuxdecoder_1_out_2));
  BranchMUXDecoder branchmuxdecoder_1 (.Op(ALUOp), .out_2(branchmuxdecoder_1_out_2));
  _16_bit_Multiplier u_16_bit_multiplier_1 (.in_1(ABus), .in_2(BBus), .in_3({16{1'b0}}), .out_4(MulOut));
  Shifter shifter_1 (.ABus(ABus), .Imm5(BBus), .ShiftOut(ShiftOut), .ShiftSel(ALUOp));
  _16_bit_ALU u_16_bit_alu_1 (.in_2(ALUOp), .out_4(ALUOut), .out_5(n16_bit_alu_1_out_5), .in_1(ABus), .in_3(BBus));
  Register #(.width(4)) register_2 (
    .D(n16_bit_alu_1_out_5), .en(CondUpdate), .Q({V, N, C, Z}), .clk(Clock_out), .clr(Reset));
  ABusSelector abusselector_1 (.AOut(AOut), .WOut(WOut), .PC(CurrPC), .ABusSel(ALUOp), .ABus(ABus));
  BBusSelector bbusselector_1 (.BOut(BOut), .Imm5(Imm5), .Imm8(Imm8), .Imm11(Imm11), .ALUBSel(ALUOp), .BBus(BBus));
  Multiplexer #(.width(16), .enable("false")) multiplexer_2 (
    .in0(ALUOut), .in1({16{1'b1}}), .out(multiplexer_2_out), .sel(ALUOp[4]));
  Multiplexer #(.width(16), .enable("false")) multiplexer_3 (
    .in0(WOut), .in1(BBus), .out(multiplexer_3_out), .sel(ALUOp[4]));
  WBusSelector wbusselector_1 (
    .ALUOut(ALUOut), .DataOut(DataOut), .ShiftOut(ShiftOut), .PC(CurrPC), .MulIn(MulOut), .WIn(WIn),
    .Op(ALUOp));
  RAM #(.addrWidth(16), .dataWidth(16), .bus("separate")) ram_2 (
    .addr(multiplexer_2_out), .din(multiplexer_3_out), .data(DataOut), .str(MemWrite), .clk(Clock_out),
    .ld(MemRead), .clr(Reset));  // open: sel

  // Other names for the same wires on the sheet: BranchPC[15:0] = ABus; CondCodes[3:0] = {V, N, C, Z}
endmodule

module _1_bit_Adder (
  input  CarryIn,
  input  A,
  input  B,
  output CarryOut,
  output Sum
);

  wire and_1_out, and_2_out, and_3_out, and_4_out, and_5_out, and_6_out, and_7_out;

  and and_1 (and_1_out, A, CarryIn);
  and and_2 (and_2_out, B, CarryIn);
  and and_3 (and_3_out, A, B);
  and and_4 (and_4_out, A, ~B, ~CarryIn);  // AND_Gate
  and and_5 (and_5_out, ~A, B, ~CarryIn);  // AND_Gate
  and and_6 (and_6_out, ~A, ~B, CarryIn);  // AND_Gate
  and and_7 (and_7_out, A, B, CarryIn);
  or or_1 (CarryOut, and_1_out, and_2_out, and_3_out);
  or or_2 (Sum, and_4_out, and_5_out, and_6_out, and_7_out);
endmodule

module _2_bit_Ripple_Adder (
  input  [1:0] A,
  input  [1:0] B,
  input  Carry_In,
  output out_4,
  output [1:0] out_5
);

  wire n1_bit_adder_2_carryout;

  _1_bit_Adder u_1_bit_adder_1 (
    .A(A[1]), .B(B[1]), .CarryIn(n1_bit_adder_2_carryout), .CarryOut(out_4), .Sum(out_5[1]));
  _1_bit_Adder u_1_bit_adder_2 (
    .A(A[0]), .B(B[0]), .CarryIn(Carry_In), .CarryOut(n1_bit_adder_2_carryout), .Sum(out_5[0]));
endmodule

module _4_bit_Adder (
  input  in_1,
  input  [3:0] in_2,
  input  [3:0] in_3,
  output out_4,
  output [3:0] out_5
);

  wire n2_bit_ripple_adder_1_out_4;

  _2_bit_Ripple_Adder u_2_bit_ripple_adder_1 (
    .B(in_3[1:0]), .Carry_In(in_1), .out_4(n2_bit_ripple_adder_1_out_4), .out_5(out_5[1:0]), .A(in_2[1:0]));
  _2_bit_Ripple_Adder u_2_bit_ripple_adder_2 (
    .B(in_3[3:2]), .Carry_In(n2_bit_ripple_adder_1_out_4), .out_4(out_4), .out_5(out_5[3:2]), .A(in_2[3:2]));
endmodule

module _16_bit_ALU (
  input  [15:0] in_1,
  input  [4:0] in_2,
  input  [15:0] in_3,
  output [15:0] out_4,
  output [3:0] out_5
);

  wire and_1_out, and_2_out, and_3_out, and_4_out, and_5_out, and_7_out, n4_bit_adder_1_out_4,
       n4_bit_adder_2_out_4, n4_bit_adder_3_out_4, nor_1_out, not_1_out, not_2_out, not_3_out, not_4_out,
       or_1_out, or_2_out, xor_1_out;
  wire [3:0] controlled_buffer_2_out, controlled_buffer_3_out, controlled_buffer_4_out,
       controlled_inverter_1_out, n4_bit_adder_2_out_5;
  wire [15:0] and_6_out, n4_bit_adder_1_out_5, or_3_out;

  not not_1 (not_1_out, in_2[3]);
  not not_2 (not_2_out, in_2[2]);
  not not_3 (not_3_out, in_2[1]);
  not not_4 (not_4_out, in_2[0]);
  assign controlled_inverter_1_out = and_2_out ? ~in_3[3:0] : 4'bz;  // Controlled_Inverter controlled_inverter_1
  _4_bit_Adder u_4_bit_adder_1 (
    .in_1(and_2_out), .in_2(in_1[3:0]), .out_4(n4_bit_adder_1_out_4), .out_5(n4_bit_adder_1_out_5[3:0]),
    .in_3(controlled_inverter_1_out));
  assign controlled_inverter_1_out = or_1_out ? in_3[3:0] : 4'bz;  // Controlled_Buffer controlled_buffer_1
  and and_1 (and_1_out, in_2[1], in_2[0]);
  assign controlled_buffer_2_out = or_1_out ? in_3[7:4] : 4'bz;  // Controlled_Buffer controlled_buffer_2
  assign controlled_buffer_2_out = and_2_out ? ~in_3[7:4] : 4'bz;  // Controlled_Inverter controlled_inverter_2
  _4_bit_Adder u_4_bit_adder_2 (
    .in_1(n4_bit_adder_1_out_4), .in_2(in_1[7:4]), .out_4(n4_bit_adder_2_out_4),
    .out_5(n4_bit_adder_2_out_5), .in_3(controlled_buffer_2_out));
  and and_2 (and_2_out, not_1_out, in_2[2], not_3_out);
  and and_3 (and_3_out, not_2_out, in_2[0]);
  and and_4 (and_4_out, in_2[1], not_4_out);
  _4_bit_Adder u_4_bit_adder_3 (
    .in_1(n4_bit_adder_2_out_4), .in_2(in_1[11:8]), .out_4(n4_bit_adder_3_out_4),
    .out_5(n4_bit_adder_1_out_5[11:8]), .in_3(controlled_buffer_3_out));
  and and_5 (and_5_out, not_1_out, not_3_out, not_4_out);
  assign controlled_buffer_3_out = or_1_out ? in_3[11:8] : 4'bz;  // Controlled_Buffer controlled_buffer_3
  assign controlled_buffer_3_out = and_2_out ? ~in_3[11:8] : 4'bz;  // Controlled_Inverter controlled_inverter_3
  assign controlled_buffer_4_out = or_1_out ? in_3[15:12] : 4'bz;  // Controlled_Buffer controlled_buffer_4
  assign controlled_buffer_4_out = and_2_out ? ~in_3[15:12] : 4'bz;  // Controlled_Inverter controlled_inverter_4
  _4_bit_Adder u_4_bit_adder_4 (
    .in_1(n4_bit_adder_3_out_4), .in_2(in_1[15:12]), .out_4(out_5[1]), .out_5(n4_bit_adder_1_out_5[15:12]),
    .in_3(controlled_buffer_4_out));
  or or_1 (or_1_out, in_2[3], and_3_out, and_1_out);
  or or_2 (or_2_out, or_1_out, and_2_out);
  assign and_6_out = in_3 & in_1;  // AND_Gate and_6, 16 bits wide
  assign out_4 = and_4_out ? and_6_out : 16'bz;  // Controlled_Buffer controlled_buffer_5
  assign or_3_out = in_1 | in_3;  // OR_Gate or_3, 16 bits wide
  assign out_4 = and_5_out ? or_3_out : 16'bz;  // Controlled_Buffer controlled_buffer_6
  xor xor_1 (xor_1_out, in_3[15], and_2_out);
  assign out_4 = or_2_out ? {n4_bit_adder_1_out_5[15:8], n4_bit_adder_2_out_5, n4_bit_adder_1_out_5[3:0]} : 16'bz;  // Controlled_Buffer controlled_buffer_7
  and and_7 (and_7_out, in_1[15], xor_1_out, ~out_4[15]);  // AND_Gate
  nor nor_1 (nor_1_out, in_1[15], xor_1_out, ~out_4[15]);  // NOR_Gate
  or or_4 (out_5[3], and_7_out, nor_1_out);
  nor nor_2 (out_5[0], out_4[7], out_4[0], out_4[1], out_4[2], out_4[3], out_4[4], out_4[5], out_4[6], out_4[8], out_4[9], out_4[10], out_4[11], out_4[12], out_4[13], out_4[14], out_4[15]);

  assign out_5[2] = out_4[15];
endmodule

module _4_bit_Multiplier (
  input  [15:0] A_16_bit,
  input  [15:0] PIn,
  input  [3:0] B_4_bit,
  output [3:0] P_4_bit,
  output [15:0] POut
);

  wire n16x1_multiplier_1_p5, n16x1_multiplier_2_p5, n16x1_multiplier_3_p5;

  // _16x1_Multiplier 16x1_multiplier_1: pin names not known; wires that end beside it: A_16_bit, B_4_bit[0], PIn, P_4_bit[0], n16x1_multiplier_1_p5
  // _16x1_Multiplier 16x1_multiplier_2: pin names not known; wires that end beside it: A_16_bit, B_4_bit[1], n16x1_multiplier_1_p5, P_4_bit[1], n16x1_multiplier_2_p5
  // _16x1_Multiplier 16x1_multiplier_3: pin names not known; wires that end beside it: A_16_bit, B_4_bit[2], n16x1_multiplier_2_p5, P_4_bit[2], n16x1_multiplier_3_p5
  // _16x1_Multiplier 16x1_multiplier_4: pin names not known; wires that end beside it: A_16_bit, B_4_bit[3], n16x1_multiplier_3_p5, P_4_bit[3], POut
endmodule

module _16_bit_Multiplier (
  input  [15:0] in_1,
  input  [15:0] in_2,
  input  [15:0] in_3,
  output [15:0] out_4
);

  wire [15:0] n4_bit_multiplier_1_pout, n4_bit_multiplier_2_pout, n4_bit_multiplier_3_pout;

  _4_bit_Multiplier u_4_bit_multiplier_1 (
    .A_16_bit(in_1), .PIn(in_3), .B_4_bit(in_2[3:0]), .P_4_bit(out_4[3:0]), .POut(n4_bit_multiplier_1_pout));
  _4_bit_Multiplier u_4_bit_multiplier_2 (
    .A_16_bit(in_1), .PIn(n4_bit_multiplier_1_pout), .B_4_bit(in_2[7:4]), .P_4_bit(out_4[7:4]),
    .POut(n4_bit_multiplier_2_pout));
  _4_bit_Multiplier u_4_bit_multiplier_3 (
    .A_16_bit(in_1), .PIn(n4_bit_multiplier_2_pout), .B_4_bit(in_2[11:8]), .P_4_bit(out_4[11:8]),
    .POut(n4_bit_multiplier_3_pout));
  _4_bit_Multiplier u_4_bit_multiplier_4 (
    .A_16_bit(in_1), .PIn(n4_bit_multiplier_3_pout), .B_4_bit(in_2[15:12]), .P_4_bit(out_4[15:12]));  // open: POut
endmodule

// Registers
module Register_File (
  input  [15:0] WData,
  input  Clk,
  input  [2:0] ASel,
  input  _0,
  input  WEn,
  input  [2:0] BSel,
  input  [2:0] WSel,
  output [15:0] ABus,
  output [15:0] BBus,
  output [15:0] WBus
);

  wire demultiplexer_1_out0, demultiplexer_1_out1, demultiplexer_1_out2, demultiplexer_1_out3,
       demultiplexer_1_out4, demultiplexer_1_out5, demultiplexer_1_out6, demultiplexer_1_out7;
  wire [15:0] register_1_q, register_2_q, register_3_q, register_4_q, register_5_q, register_6_q,
       register_7_q, register_8_q;

  Demultiplexer #(.select(3), .enable("false")) demultiplexer_1 (
    .out0(demultiplexer_1_out0), .out1(demultiplexer_1_out1), .out2(demultiplexer_1_out2),
    .out3(demultiplexer_1_out3), .out4(demultiplexer_1_out4), .out5(demultiplexer_1_out5),
    .out6(demultiplexer_1_out6), .out7(demultiplexer_1_out7), .in(WEn), .sel(WSel));
  Register #(.width(16)) register_1 (.D(WData), .en(demultiplexer_1_out0), .Q(register_1_q), .clk(Clk), .clr(_0));
  Register #(.width(16)) register_2 (.D(WData), .en(demultiplexer_1_out1), .Q(register_2_q), .clk(Clk), .clr(_0));
  Register #(.width(16)) register_3 (.D(WData), .en(demultiplexer_1_out2), .Q(register_3_q), .clk(Clk), .clr(_0));
  Register #(.width(16)) register_4 (.D(WData), .en(demultiplexer_1_out3), .Q(register_4_q), .clk(Clk), .clr(_0));
  Register #(.width(16)) register_5 (.D(WData), .en(demultiplexer_1_out4), .Q(register_5_q), .clk(Clk), .clr(_0));
  Register #(.width(16)) register_6 (.D(WData), .en(demultiplexer_1_out5), .Q(register_6_q), .clk(Clk), .clr(_0));
  Register #(.width(16)) register_7 (.D(WData), .en(demultiplexer_1_out6), .Q(register_7_q), .clk(Clk), .clr(_0));
  Register #(.width(16)) register_8 (.D(WData), .en(demultiplexer_1_out7), .Q(register_8_q), .clk(Clk), .clr(_0));
  Multiplexer #(.select(3), .width(16), .enable("false")) multiplexer_1 (
    .in0(register_1_q), .in1(register_2_q), .in2(register_3_q), .in3(register_4_q), .in4(register_5_q),
    .in5(register_6_q), .in6(register_7_q), .in7(register_8_q), .out(ABus), .sel(ASel));
  Multiplexer #(.select(3), .width(16), .enable("false")) multiplexer_2 (
    .in0(register_1_q), .in1(register_2_q), .in2(register_3_q), .in3(register_4_q), .in4(register_5_q),
    .in5(register_6_q), .in6(register_7_q), .in7(register_8_q), .out(BBus), .sel(BSel));
  Multiplexer #(.select(3), .width(16), .enable("false")) multiplexer_3 (
    .in0(register_1_q), .in1(register_2_q), .in2(register_3_q), .in3(register_4_q), .in4(register_5_q),
    .in5(register_6_q), .in6(register_7_q), .in7(register_8_q), .out(WBus), .sel(WSel));
endmodule

module Decoder (
  input  [15:0] Inst,
  output Cond__Update,
  output [4:0] ALUOp,
  output MemRead,
  output MemWrite,
  output RegWrite,
  output [10:0] Imm11,
  output [2:0] WSel,
  output [2:0] ASel,
  output [2:0] BSel,
  output [4:0] Imm5,
  output [7:0] Imm8
);

  wire and_1_out, and_2_out, and_3_out, and_4_out, and_6_out, and_7_out, and_8_out, and_9_out, and_10_out,
       and_11_out, and_12_out, and_13_out, and_14_out;

  and and_1 (and_1_out, Inst[11], ~Inst[12], ~Inst[14]);  // AND_Gate
  and and_2 (and_2_out, ~Inst[11], ~Inst[13], ~Inst[14]);  // AND_Gate
  and and_3 (and_3_out, ~Inst[15], ~Inst[13], ~Inst[12], Inst[11]);  // AND_Gate
  and and_4 (and_4_out, ~Inst[11], ~Inst[12], Inst[13], Inst[14], ~Inst[15]);  // AND_Gate
  and and_5 (MemRead, Inst[11], Inst[12], Inst[13], ~Inst[15]);  // AND_Gate
  and and_6 (and_6_out, ~Inst[15], ~Inst[13], Inst[12], Inst[11]);  // AND_Gate
  and and_7 (and_7_out, Inst[11], Inst[12], Inst[13], Inst[14], Inst[15]);
  and and_8 (and_8_out, ~Inst[11], Inst[12], ~Inst[14]);  // AND_Gate
  and and_9 (and_9_out, ~Inst[14], Inst[13], Inst[12]);  // AND_Gate
  and and_10 (and_10_out, ~Inst[11], Inst[15], ~Inst[14]);  // AND_Gate
  and and_11 (and_11_out, ~Inst[12], ~Inst[13], ~Inst[15]);  // AND_Gate
  and and_12 (and_12_out, Inst[12], ~Inst[15], ~Inst[11]);  // AND_Gate
  and and_13 (and_13_out, ~Inst[15], Inst[13], Inst[14]);  // AND_Gate
  or or_1 (MemWrite, and_6_out, and_7_out);
  and and_14 (and_14_out, Inst[11], ~Inst[12], ~Inst[13], ~Inst[14], Inst[15]);  // AND_Gate
  or or_2 (RegWrite, and_8_out, and_9_out, and_10_out, and_14_out, and_11_out, and_12_out, and_13_out);
  or or_3 (Cond__Update, and_1_out, and_2_out, and_3_out, and_4_out);

  assign ALUOp = Inst[15:11];
  assign ASel = Inst[7:5];
  assign BSel = Inst[4:2];
  assign Imm5 = Inst[4:0];
  assign Imm8 = Inst[7:0];
  assign Imm11 = Inst[10:0];
  assign WSel = Inst[10:8];

  // Other names for the same wires on the sheet: OpCode[4:0] = Inst[15:11]
endmodule

module PC_Control_Unit (
  input  [15:0] CurPC,
  input  [15:0] Imm,
  input  PCSel,
  output [15:0] NextPC
);

  wire [15:0] adder_1_out, adder_2_out;

  Adder #(.width(16)) adder_1 (.a(CurPC), .b(16'h1), .out(adder_1_out));  // open: cin, cout
  Adder #(.width(16)) adder_2 (.a(CurPC), .b(Imm), .out(adder_2_out));  // open: cin, cout
  Multiplexer #(.width(16), .enable("false")) multiplexer_1 (
    .in0(adder_1_out), .in1(adder_2_out), .out(NextPC), .sel(PCSel));
endmodule

module ABusSelector (
  input  [15:0] AOut,
  input  [15:0] WOut,
  input  [15:0] PC,
  input  [4:0] ABusSel,
  output [15:0] ABus
);

  wire [1:0] abusmuxdecoder_1_output;
  wire [15:0] not_1_out;

  assign not_1_out = ~AOut;  // NOT_Gate not_1, 16 bits wide
  Multiplexer #(.select(2), .width(16), .enable("false")) multiplexer_1 (
    .in0(AOut), .in1(not_1_out), .in2(WOut), .in3(PC), .out(ABus), .sel(abusmuxdecoder_1_output));
  ABusMUXDecoder abusmuxdecoder_1 (.OpCode(ABusSel), .Output(abusmuxdecoder_1_output));
endmodule

module ABusMUXDecoder (
  input  [4:0] OpCode,
  output [1:0] Output
);

  wire and_1_out, and_2_out, and_3_out;

  and and_1 (and_1_out, OpCode[3], OpCode[2], ~OpCode[1], ~OpCode[0]);  // AND_Gate
  and and_2 (and_2_out, OpCode[4], OpCode[3]);
  and and_3 (and_3_out, OpCode[4], OpCode[1], OpCode[0]);
  or or_1 (Output[0], and_1_out, and_2_out, and_3_out);

  assign Output[1] = OpCode[4];
endmodule

module BBusSelector (
  input  [15:0] BOut,
  input  [4:0] Imm5,
  input  [7:0] Imm8,
  input  [4:0] ALUBSel,
  input  [10:0] Imm11,
  output [15:0] BBus
);

  wire [2:0] bbusmuxdecoder_1_out;
  wire [15:0] bit_extender_1_out, bit_extender_2_out, bit_extender_3_out, bit_extender_4_out,
       bit_extender_5_out;

  assign bit_extender_1_out = {{11{Imm5[4]}}, Imm5};  // Bit_Extender bit_extender_1
  assign bit_extender_2_out = {{8{Imm8[7]}}, Imm8};  // Bit_Extender bit_extender_2
  assign bit_extender_3_out = {{8{1'b0}}, Imm8};  // Bit_Extender bit_extender_3
  assign bit_extender_4_out = {{8{1'b1}}, Imm8};  // Bit_Extender bit_extender_4
  assign bit_extender_5_out = {{5{Imm11[10]}}, Imm11};  // Bit_Extender bit_extender_5
  Multiplexer #(.select(3), .width(16), .enable("false")) multiplexer_1 (
    .in0(BOut), .in1(bit_extender_1_out), .in2(bit_extender_2_out), .in3(bit_extender_3_out),
    .in4(bit_extender_4_out), .in5(bit_extender_5_out), .in6({16{1'b0}}), .out(BBus),
    .sel(bbusmuxdecoder_1_out));  // open: in7
  BBusMUXDecoder bbusmuxdecoder_1 (.OpCode(ALUBSel), .Out(bbusmuxdecoder_1_out));
endmodule

module BBusMUXDecoder (
  input  [4:0] OpCode,
  output [2:0] Out
);

  wire and_1_out, and_2_out, and_3_out, and_4_out, and_5_out, and_6_out, and_7_out, and_8_out, and_9_out,
       and_10_out, and_11_out, and_12_out;

  and and_1 (and_1_out, ~OpCode[0], ~OpCode[1], OpCode[4]);  // AND_Gate
  and and_2 (and_2_out, OpCode[3], OpCode[4]);
  and and_3 (and_3_out, OpCode[1], OpCode[3]);
  and and_4 (and_4_out, OpCode[3], ~OpCode[0]);  // AND_Gate
  and and_5 (and_5_out, OpCode[3], ~OpCode[2]);  // AND_Gate
  and and_6 (and_6_out, OpCode[4], ~OpCode[2], ~OpCode[1]);  // AND_Gate
  and and_7 (and_7_out, ~OpCode[3], OpCode[2], ~OpCode[1], ~OpCode[0]);  // AND_Gate
  and and_8 (and_8_out, ~OpCode[4], OpCode[3], OpCode[2], ~OpCode[1], OpCode[0]);  // AND_Gate
  and and_9 (and_9_out, OpCode[4], ~OpCode[3], OpCode[2]);  // AND_Gate
  and and_10 (and_10_out, OpCode[4], ~OpCode[3], ~OpCode[1]);  // AND_Gate
  and and_11 (and_11_out, ~OpCode[4], ~OpCode[3], OpCode[2], ~OpCode[1], ~OpCode[0]);  // AND_Gate
  and and_12 (and_12_out, OpCode[4], ~OpCode[2], OpCode[1]);  // AND_Gate
  or or_1 (Out[1], and_7_out, and_8_out, and_9_out, and_10_out);
  or or_2 (Out[0], and_1_out, and_2_out, and_3_out, and_4_out, and_5_out, and_6_out);
  or or_3 (Out[2], and_2_out, and_8_out, and_11_out, and_12_out);
endmodule

module WBusSelector (
  input  [15:0] ALUOut,
  input  [15:0] DataOut,
  input  [15:0] ShiftOut,
  input  [15:0] PC,
  input  [4:0] Op,
  input  [15:0] MulIn,
  output [15:0] WIn
);

  wire [2:0] wbusmuxdecoder_1_out;
  wire [15:0] adder_1_out;

  Adder #(.width(16)) adder_1 (.a(PC), .b(16'h1), .out(adder_1_out));  // open: cin, cout
  Multiplexer #(.select(3), .width(16), .enable("false")) multiplexer_1 (
    .in0(ALUOut), .in1(DataOut), .in2(ShiftOut), .in3(adder_1_out), .in4(MulIn), .in5(MulIn), .in6(MulIn),
    .in7(MulIn), .out(WIn), .sel(wbusmuxdecoder_1_out));
  WBusMUXDecoder wbusmuxdecoder_1 (.Op(Op), .Out(wbusmuxdecoder_1_out));
endmodule

module WBusMUXDecoder (
  input  [4:0] Op,
  output [2:0] Out
);

  wire and_2_out, and_3_out, and_4_out, and_5_out, and_6_out, and_7_out;

  and and_1 (Out[0], Op[2], Op[0]);
  and and_2 (and_2_out, Op[2], ~Op[1], Op[0]);  // AND_Gate
  and and_3 (and_3_out, Op[3], ~Op[2], ~Op[0]);  // AND_Gate
  and and_4 (and_4_out, Op[2], Op[1], ~Op[0]);  // AND_Gate
  and and_5 (and_5_out, Op[4], Op[2]);
  and and_6 (and_6_out, ~Op[4], ~Op[3], Op[2], Op[1], ~Op[0]);  // AND_Gate
  and and_7 (and_7_out, Op[0], ~Op[1], ~Op[2], ~Op[3], Op[4]);  // AND_Gate
  or or_1 (Out[1], and_2_out, and_3_out, and_4_out, and_5_out);
  or or_2 (Out[2], and_6_out, and_7_out);
endmodule

module Shifter (
  input  [15:0] ABus,
  input  [15:0] Imm5,
  input  [4:0] ShiftSel,
  output [15:0] ShiftOut
);

  wire [0:0] and_1_out;
  wire [3:0] multiplexer_1_out;
  wire [15:0] bit_extender_1_out, multiplexer_2_out, or_1_out, shifter_1_out, shifter_2_out, shifter_3_out,
       shifter_4_out;

  Multiplexer #(.width(4), .enable("false")) multiplexer_1 (
    .in0(4'b0000), .in1(4'b1000), .out(multiplexer_1_out), .sel(ShiftSel[1]));
  assign bit_extender_1_out = {{8{1'b0}}, ABus[7:0]};  // Bit_Extender bit_extender_1
  Shifter_part #(.width(16)) shifter_1 (.in(Imm5), .\dist (multiplexer_1_out), .out(shifter_1_out));
  Shifter_part #(.width(16), .shift("ar")) shifter_2 (.in(ABus), .\dist (Imm5[3:0]), .out(shifter_2_out));
  Shifter_part #(.width(16), .shift("lr")) shifter_3 (.in(ABus), .\dist (Imm5[3:0]), .out(shifter_3_out));
  Shifter_part #(.width(16), .shift("rr")) shifter_4 (.in(ABus), .\dist (Imm5[3:0]), .out(shifter_4_out));
  assign or_1_out = bit_extender_1_out | shifter_1_out;  // OR_Gate or_1, 16 bits wide
  Multiplexer #(.width(16), .enable("false")) multiplexer_2 (
    .in0(shifter_1_out), .in1(or_1_out), .out(multiplexer_2_out), .sel(ShiftSel[1]));
  Multiplexer #(.select(2), .width(16), .enable("false")) multiplexer_3 (
    .in0(shifter_2_out), .in1(shifter_3_out), .in2(multiplexer_2_out), .in3(shifter_4_out), .out(ShiftOut),
    .sel({ShiftSel[2], and_1_out[0]}));
  and and_1 (and_1_out[0], ~ShiftSel[4], ShiftSel[1]);  // AND_Gate

  // Other names for the same wires on the sheet: En = ShiftSel[1]
endmodule

module BranchEnableUnit (
  input  [3:0] CondCodes__ZCNV,
  input  [2:0] BrType,
  input  BranchReq,
  output out_4
);

  wire and_1_out, and_2_out, and_3_out, and_4_out, and_5_out, and_6_out, and_7_out, and_8_out, and_9_out,
       and_10_out, and_11_out, and_12_out, and_13_out, and_14_out, and_15_out, not_1_out, not_2_out,
       or_1_out, xnor_1_out;

  and and_1 (and_1_out, ~BrType[0], ~BrType[1], ~BrType[2]);  // AND_Gate
  and and_2 (and_2_out, BrType[0], ~BrType[1], ~BrType[2]);  // AND_Gate
  and and_3 (and_3_out, ~BrType[0], BrType[1], ~BrType[2]);  // AND_Gate
  and and_4 (and_4_out, BrType[0], BrType[1], ~BrType[2]);  // AND_Gate
  and and_5 (and_5_out, ~BrType[0], ~BrType[1], BrType[2]);  // AND_Gate
  and and_6 (and_6_out, BrType[0], ~BrType[1], BrType[2]);  // AND_Gate
  and and_7 (and_7_out, ~BrType[0], BrType[1], BrType[2]);  // AND_Gate
  and and_8 (and_8_out, BrType[0], BrType[1], BrType[2]);
  xnor xnor_1 (xnor_1_out, CondCodes__ZCNV[3], CondCodes__ZCNV[2]);
  and and_9 (and_9_out, CondCodes__ZCNV[0], and_3_out);
  and and_10 (and_10_out, and_2_out, ~CondCodes__ZCNV[0], xnor_1_out);  // AND_Gate
  and and_11 (and_11_out, xnor_1_out, and_4_out);
  not not_1 (not_1_out, xnor_1_out);
  and and_12 (and_12_out, not_1_out, and_5_out);
  and and_13 (and_13_out, ~CondCodes__ZCNV[0], and_6_out);  // AND_Gate
  and and_14 (and_14_out, ~CondCodes__ZCNV[0], xnor_1_out);  // AND_Gate
  not not_2 (not_2_out, and_14_out);
  or or_1 (or_1_out, and_1_out, and_10_out, and_12_out, and_11_out, and_13_out, and_9_out, and_8_out, and_15_out);
  and and_15 (and_15_out, not_2_out, and_7_out);
  and and_16 (out_4, BranchReq, or_1_out);
endmodule

module BranchRequestUnit (
  input  [4:0] Op,
  output BrReq,
  output [2:0] BrType
);

  wire and_1_out, and_2_out;

  and and_1 (and_1_out, Op[4], Op[3]);
  and and_2 (and_2_out, Op[4], ~Op[3], Op[1], Op[0]);  // AND_Gate
  or or_1 (BrReq, and_1_out, and_2_out);

  assign BrType = Op[2:0];
endmodule

module BranchMUXDecoder (
  input  [4:0] Op,
  output out_2
);

  wire and_1_out, and_2_out, and_3_out;

  and and_1 (and_1_out, ~Op[4], ~Op[3], Op[2], ~Op[1], ~Op[0]);  // AND_Gate
  or or_1 (out_2, and_1_out, and_2_out, and_3_out);
  and and_2 (and_2_out, ~Op[4], Op[3], Op[2], ~Op[1], Op[0]);  // AND_Gate
  and and_3 (and_3_out, Op[4], Op[3], Op[2], Op[1], Op[0]);
endmodule
